# Fritzing sketch schematics (saved by Fritzing 0.9.3b)
circuit board: 7.14762cm x 4.63193cm
breadboards: 1

parts:
  U1 = Voltage Regulator - 5V [package="TO220 [THT]"]
  U2 = atmega328 [package=dip]
  J1 = Power Jack [package=power_jack_smd]
  R2 = PHOTOCELL [package=photocell]
  PIR1 = PIR sensor
  Q1 = MOSFET-NCHANNEL [package=to220v]
  J2 = Power Jack [package=power_jack_smd]
  S1 = Momentary Switch [package=ksa_sealed_tac_switch]
  R1 = Resistor [tolerance=±5% resistance=220 package=THT]
  R4 = Resistor [tolerance=±5% resistance=1.5k package=THT]
  R5 = Resistor [tolerance=±5% resistance=1.5k package=THT]
  LED1 = 7-SEGMENT-4DIGIT-YOUNGSUN [package=7-segment-4digit-youngsun-longpads]
  S3 = Momentary Switch [package=ksa_sealed_tac_switch]

nets (from the breadboard view):
  N1: U1.input_voltage, J1.PWR, J2.PWR
  GND: U1.GND, U2.GND, J1.GND, PIR1.GND, Q1.S, R1.Pin_1, R4.Pin_0, R5.Pin_0
  VCC: U1.output_voltage, U2.VCC, U2.AVCC, R2.P$1, PIR1.VDD, S1.2, S3.3
  N2: U2.D2, S1.4, R4.Pin_1
  N3: U2.D3_(PWM), S3.1
  N4: U2.D4, LED1.DP
  N5: U2.D5_(PWM), LED1.C
  N6: U2.D6_(PWM), LED1.D
  N7: U2.D7, LED1.E
  N8: U2.D8, LED1.F
  N9: U2.D9_(PWM), Q1.G
  N10: U2.D10_(PWM), LED1.G
  N11: U2.D11_(PWM), LED1.B
  N12: U2.D12, LED1.A
  N13: U2.A0, LED1.DIG4
  N14: U2.A1, PIR1.SIG
  N15: U2.A2, R2.P$2, R1.Pin_0
  N16: U2.A3, LED1.DIG3
  N17: Q1.D, J2.GND

notes:
  in the hall
  to the led stripe
  12V power
  add 10 minutes
  change brightness
